# Fritzing sketch 32color1 (saved by Fritzing 0.9.3b)

parts:
  U1 = ESP32S-HiLetgo [part_number=ESP32S-HiLetgo]
  R1 = 220 Ω Resistor [package=THT]

nets:
  N1: U1.3.3, R1.VCC
  N2: U1.GPIO4, R1.BUSY
  N3: U1.GPIO16, R1.RST
  N4: U1.GPIO17, R1.DC
  N5: U1.GPIO5, R1.CS
  N6: U1.GPIO18, R1.CLK
  N7: U1.GPIO23, R1.DIN
  GND: U1.GND, R1.GND

custom parts:
  ESP32S-HiLetgo: HiLetgo ESP-WROOM-32 ESP32 ESP-32S Development Board 2.4GHz Dual-Mode WiFi + Bluetooth Dual Cores Microcontroller The ESP32 integrated with Antenna switches, RF Balun, power amplifiers, low-noise amplifiers, filters, and management modules, and the entire solution occupies the least area of PCB. 2.4 GHz Wi-Fi plus Bluetooth dual-mode chip, with TSMC Ultra-low power consumption 40nm technology,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
  220 Ω Resistor: A generic resistor (0.25W)
